# Fritzing sketch z-axes-connectors (saved by Fritzing 0.9.3b)
stripboards: 4

parts:
  J2 = female pin header, 4 pins [form="♀ (female)"]
  Power_plug1 = Power plug
  J3 = female pin header, 2 pins [form="♀ (female)"]
  J4 = female pin header, 4 pins [form="♀ (female)"]
  J5 = female pin header, 2 pins [form="♀ (female)"]
  J7 = female pin header, 4 pins [form="♀ (female)"]
  J8 = female pin header, 4 pins [form="♀ (female)"]
  J9 = female pin header, 2 pins [form="♀ (female)"]
  J10 = female pin header, 2 pins [form="♀ (female)"]
  J11 = female pin header, 3 pins [form="♀ (female)"]
  J12 = female pin header, 3 pins [form="♀ (female)"]
  J13 = female pin header, 5 pins [form="♀ (female)"]
  J14 = female pin header, 2 pins [form="♀ (female)"]
  J15 = female pin header, 2 pins [form="♀ (female)"]
  J16 = female pin header, 5 pins [form="♀ (female)"]
  J6 = female pin header, 1 pin [form="♀ (female)"]
  Part2 = Arduino Mega 2560 (Rev3)  # not connected
  Part3 = Arduino Due (Rev2b)
  Part5 = Arduino Ethernet Shield (Rev3)  # not connected
  Part6 = RAMPS 1.4 Shield for Arduino Mega 2560
  proto1 = Adafruit_PermaProto_1_4_Board
  Part8 = Logic Level Converter  # not connected
  J17 = female pin header, 2 pins [form="♀ (female)"]  # not connected
  OLED1 = OLED 128x64 I2C Monochrome Display
  J18 = female pin header, 7 pins [form="♀ (female)"]  # not connected
  J19 = female pin header, 7 pins [form="♀ (female)"]  # not connected
  J20 = female pin header, 2 pins [form="♀ (female)"]  # not connected
  Part9 = BME280 Breakout
  Part10 = Thumb Joystick
  J23 = female pin header, 7 pins [form="♀ (female)"]  # not connected
  J24 = female pin header, 7 pins [form="♀ (female)"]  # not connected
  J21 = female pin header, 3 pins [form="♀ (female)"]  # not connected
  J22 = female pin header, 3 pins [form="♀ (female)"]  # not connected
  J25 = female pin header, 3 pins [form="♀ (female)"]  # not connected
  J26 = female pin header, 3 pins [form="♀ (female)"]  # not connected
  U1 = LCD-16X2 [package=lcd-16x2]
  R1 = Resistor [tolerance=±5% resistance=330 package=THT]
  R3 = Trimmer Potentiometer [maximum_resistance=10kΩ package=THT]
  J28 = female pin header, 2 pins [form="♀ (female)"]
  J27 = female pin header, 6 pins [form="♀ (female)"]

nets:
  N1: J2.pin1, J13.pin3, J16.pin3
  N2: J2.pin2, J3.pin1, J4.pin2
  N3: J2.pin3, J3.pin2, J4.pin3
  N4: J2.pin4, Power_plug1.VCC, J4.pin4
  N5: J4.pin1, J5.pin1, J6.pin1
  N6: J5.pin2, J13.pin4, J16.pin4
  N7: J7.pin1, J8.pin1
  N8: J7.pin2, J8.pin2
  N9: J7.pin3, J8.pin3
  N10: J7.pin4, J8.pin4
  N11: J9.pin1, J10.pin1, J11.pin1, J12.pin1
  N12: J9.pin2, J10.pin2, J11.pin2, J12.pin2
  N13: J11.pin3, J12.pin3, J13.pin2, J16.pin2
  N14: J13.pin1, J15.pin1, J16.pin1
  N15: J13.pin5, J14.pin2, J16.pin5
  N16: J14.pin1, J15.pin2
  N17: Part3.A0, Part10.HORZ
  N18: Part3.A1, Part10.VERT
  N19: Part3.A2, Part10.SEL
  N20: Part3.D16/TX2, proto1.connectorA12
  N21: Part3.D17/RX2, proto1.connectorA13
  N22: Part3.D20/SDA3, proto1.connectorA8
  N23: Part3.D21/SCL3, proto1.connectorA9
  N24: Part3.IOREF, proto1.connectorW15
  N25: Part3.5V, proto1.connectorY15
  N26: Part3.GND, Part6.5A-, proto1.connectorX15
  N27: Part3.VIN, Part6.5A+
  N28: Part3.SDA1, OLED1.SDA
  N29: Part3.SCL1, OLED1.SCK
  N30: Part6.5V/AUX2, U1.VDD, R1.Pin_0, R3.leg1, J28.pin2
  N31: Part6.D21/SCL, proto1.connectorJ9
  N32: Part6.D20/SDA, proto1.connectorJ8
  N33: Part6.GND/AUX2, U1.VSS, U1.R_W, U1.K, R3.leg2, J28.pin1
  N34: Part6.D0, proto1.connectorJ13
  N35: Part6.D1, proto1.connectorJ12
  N36: Part6.D23/LCD_Header, U1.RS, J27.pin1
  N37: Part6.D25/LCD_Header, U1.E, J27.pin2
  N38: Part6.D27/LCD_Header, U1.DB4, J27.pin3
  N39: Part6.D29/LCD_Header, U1.DB5, J27.pin4
  N40: Part6.D31/LCD_Header, U1.DB6, J27.pin5
  N41: Part6.D33/LCD_Header, U1.DB7, J27.pin6
  N42: proto1.connectorA4, proto1.connectorC8
  N43: proto1.connectorA5, proto1.connectorD9
  N44: proto1.connectorA10, proto1.connectorW10
  N45: proto1.connectorA11, proto1.connectorX11
  N46: proto1.connectorD4, Part9.SDI/SDA
  N47: proto1.connectorD5, Part9.SCK/SCL
  N48: proto1.connectorE4, proto1.connectorF4
  N49: proto1.connectorE5, proto1.connectorF5
  N50: proto1.connectorJ10, proto1.connectorY10
  N51: proto1.connectorJ11, proto1.connectorZ11
  N52: proto1.connectorW1, OLED1.VDD
  N53: proto1.connectorW2, Part9.3.3V
  N54: proto1.connectorW5, Part10.VCC
  N55: proto1.connectorX1, OLED1.GND
  N56: proto1.connectorX2, Part9.GND
  N57: proto1.connectorX5, Part10.GND
  N58: proto1.connectorX14, proto1.connectorZ14
  N59: U1.VO, R3.wiper
  N60: U1.A, R1.Pin_1

notes:
  SCL -> Green
  SDA -> Yellow
  Motor Out
  SCL/SDA
  TOF
  5V
  Air
  AIR
  D10
  Spindle
  Laser
  +
  -
  PWM
  SW1
  SW2

custom parts:
  RAMPS 1.4 Shield for Arduino Mega 2560: This ia standard Ramps 1.4 shield which is also compatible with versions 1.5 and 1.6 of the Ramps board. This model is intended only for the breadboard view, as the schematic and PCB views are not entirely accurate.
